// Digital circuit arithmetic&logic.dig as structural Verilog
module arithmetic_logic (
  input  A7,
  input  A6,
  input  A5,
  input  A4,
  input  A3,
  input  A2,
  input  A1,
  input  A0,
  input  B7,
  input  B6,
  input  B5,
  input  B4,
  input  B3,
  input  B2,
  input  B1,
  input  B0,
  input  S,
  input  Ci,
  output O7,
  output O6,
  output O5,
  output O4,
  output O3,
  output O2,
  output O1,
  output O0,
  output Co,
  output Z
);

  wire _8bitaddersubstractor_1_co;

  _8bitAdderSubstractor _8bitaddersubstractor_1 (
    .A7(A7), .A6(A6), .A5(A5), .A4(A4), .A3(A3), .A2(A2), .A1(A1), .A0(A0), .B7(B7), .B6(B6), .B5(B5),
    .B4(B4), .B3(B3), .B2(B2), .B1(B1), .B0(B0), .S(S), .Ci(Ci), .O7(O7), .O6(O6), .O5(O5), .O4(O4), .O3(O3),
    .O2(O2), .O1(O1), .O0(O0), .Co(_8bitaddersubstractor_1_co));
  and and_1 (Z, ~O7, ~O6, ~O5, ~O4, ~O3, ~O2, ~O1, ~O0);  // And
  and and_2 (Co, _8bitaddersubstractor_1_co, ~Z);  // And
endmodule
