// Digital circuit computer.dig as structural Verilog
module computer (
  input  I7,
  input  I6,
  input  I5,
  input  I4,
  input  I3,
  input  I2,
  input  I1,
  input  I0,
  input  Num,
  input  Str,
  input  Sub,
  input  P,
  output O7,
  output O6,
  output O5,
  output O4,
  output O3,
  output O2,
  output O1,
  output O0,
  output N,
  output Z,
  output C
);

  cpu cpu_1 (
    .I7(I7), .I6(I6), .I5(I5), .I4(I4), .I3(I3), .I2(I2), .I1(I1), .I0(I0), .Num(Num), .Str(Str), .Sub(Sub),
    .P(P), .O7(O7), .O6(O6), .O5(O5), .O4(O4), .O3(O3), .O2(O2), .O1(O1), .O0(O0), .N(N), .Z(Z), .C(C));
endmodule
