// Digital circuit cpu.dig as structural Verilog
module cpu (
  input  I7,
  input  I6,
  input  I5,
  input  I4,
  input  I3,
  input  I2,
  input  I1,
  input  I0,
  input  Num,
  input  Str,
  input  Sub,
  input  P,
  output O7,
  output O6,
  output O5,
  output O4,
  output O3,
  output O2,
  output O1,
  output O0,
  output N,
  output Z,
  output C
);

  wire _8bitregister_1_d0, _8bitregister_1_d1, _8bitregister_1_d2, _8bitregister_1_d3, _8bitregister_1_d4,
       _8bitregister_1_d5, _8bitregister_1_d6, _8bitregister_1_d7, _8bitregister_2_d0, _8bitregister_2_d1,
       _8bitregister_2_d2, _8bitregister_2_d3, _8bitregister_2_d4, _8bitregister_2_d5, _8bitregister_2_d6,
       _8bitregister_2_d7, and_1_out, and_2_out, dataflipflop_1_d, not_1_out;

  not not_1 (not_1_out, Num);
  and and_1 (and_1_out, Str, not_1_out);
  and and_2 (and_2_out, Str, Num);
  _8bitRegister _8bitregister_1 (
    .I7(I7), .I6(I6), .I5(I5), .I4(I4), .I3(I3), .I2(I2), .I1(I1), .I0(I0), .S(and_1_out), .P(P),
    .D7(_8bitregister_1_d7), .D6(_8bitregister_1_d6), .D5(_8bitregister_1_d5), .D4(_8bitregister_1_d4),
    .D3(_8bitregister_1_d3), .D2(_8bitregister_1_d2), .D1(_8bitregister_1_d1), .D0(_8bitregister_1_d0));
  _8bitRegister _8bitregister_2 (
    .I7(I7), .I6(I6), .I5(I5), .I4(I4), .I3(I3), .I2(I2), .I1(I1), .I0(I0), .S(and_2_out), .P(P),
    .D7(_8bitregister_2_d7), .D6(_8bitregister_2_d6), .D5(_8bitregister_2_d5), .D4(_8bitregister_2_d4),
    .D3(_8bitregister_2_d3), .D2(_8bitregister_2_d2), .D1(_8bitregister_2_d1), .D0(_8bitregister_2_d0));
  dataFlipFlop dataflipflop_1 (.I(C), .P(P), .D(dataflipflop_1_d));
  arithmetic_logic arithmetic_logic_1 (
    .A7(_8bitregister_1_d7), .A6(_8bitregister_1_d6), .A5(_8bitregister_1_d5), .A4(_8bitregister_1_d4),
    .A3(_8bitregister_1_d3), .A2(_8bitregister_1_d2), .A1(_8bitregister_1_d1), .A0(_8bitregister_1_d0),
    .B7(_8bitregister_2_d7), .B6(_8bitregister_2_d6), .B5(_8bitregister_2_d5), .B4(_8bitregister_2_d4),
    .B3(_8bitregister_2_d3), .B2(_8bitregister_2_d2), .B1(_8bitregister_2_d1), .B0(_8bitregister_2_d0),
    .S(Sub), .Ci(dataflipflop_1_d), .O7(O7), .O6(O6), .O5(O5), .O4(O4), .O3(O3), .O2(O2), .O1(O1), .O0(O0),
    .Co(C), .N(N), .Z(Z));
endmodule
